# Fritzing sketch MainComputeUnit (saved by Fritzing 0.9.3b)
circuit board: 11cm x 10cm
breadboards: 1

parts:
  Power_Supply = double row female pin header, 40 pins [form="♀ (female)"]
  RPI = Raspberry Pi 3 [part_number=RPI-3-V1.2]
  LED1 = smd LED [color="Orange (620nm)" part_number=Power package="1206 [SMD]"]
  R1 = Resistor [tolerance=±5% resistance=220 package="0805 [SMD]"]
  Power_In = Molex 4PinB
  Remote_Display = double row male pin header, 16 pins [form="♂ (male)"]
  Data_Lines = double row female pin header, 40 pins [form="♀ (female)"]
  C3 = RUBYCON Elko
  C1 = RUBYCON Elko
  C4 = RUBYCON Elko
  C2 = RUBYCON Elko

nets:
  GND: Power_Supply.pin1, Power_Supply.pin2, Power_Supply.pin3, Power_Supply.pin4, Power_Supply.pin5, Power_Supply.pin6, Power_Supply.pin35, Power_Supply.pin36, Power_Supply.pin37, Power_Supply.pin38, Power_Supply.pin39, Power_Supply.pin40, RPI.GND, LED1.cathode, Power_In.GND, Remote_Display.pin7, Remote_Display.pin8, Remote_Display.pin9, Remote_Display.pin10, C3.minus, C1.minus, C4.minus, C2.minus
  -24V: Power_Supply.pin7, Power_Supply.pin8, Power_Supply.pin9, Power_Supply.pin10, Power_Supply.pin11, Power_Supply.pin30, Power_Supply.pin31, Power_Supply.pin32, Power_Supply.pin33, Power_Supply.pin34, Power_In.200V_GND
  24V: Power_Supply.pin12, Power_Supply.pin13, Power_Supply.pin14, Power_Supply.pin15, Power_Supply.pin16, Power_Supply.pin25, Power_Supply.pin26, Power_Supply.pin27, Power_Supply.pin28, Power_Supply.pin29, Power_In.200V_max
  5V: Power_Supply.pin17, Power_Supply.pin18, Power_Supply.pin19, Power_Supply.pin20, Power_Supply.pin21, Power_Supply.pin22, Power_Supply.pin23, Power_Supply.pin24, RPI.5V, Power_In.5V, Remote_Display.pin1, Remote_Display.pin16, C3.plus, C1.plus, C4.plus, C2.plus
  3.3V: RPI.3v3, RPI.3V3, R1.Pin_1, Remote_Display.pin2, Remote_Display.pin15
  I2C_SDA: RPI.GPIO2, Remote_Display.pin3, Data_Lines.pin15, Data_Lines.pin26
  I2C_SCLK: RPI.GPIO3, Remote_Display.pin14, Data_Lines.pin16, Data_Lines.pin25
  I2C_RST: RPI.GIPO4, Remote_Display.pin4
  GPIO17: RPI.GIPO17, Data_Lines.pin30
  GPIO27: RPI.GIPO27, Data_Lines.pin29
  GPIO22: RPI.GIPO22, Data_Lines.pin28
  SPI_MOSI: RPI.GIPO10, Data_Lines.pin19, Data_Lines.pin22
  SPI_MISO: RPI.GIPO9, Data_Lines.pin20, Data_Lines.pin21
  SPI_SCLK: RPI.GIPO11, Data_Lines.pin18, Data_Lines.pin23
  Address1: RPI.GIPO5, Data_Lines.pin3, Data_Lines.pin38
  Address2: RPI.GIPO6, Data_Lines.pin4, Data_Lines.pin37
  Address3: RPI.GIPO13, Data_Lines.pin5, Data_Lines.pin36
  Address4: RPI.GIPO19, Data_Lines.pin6, Data_Lines.pin35
  Address5: RPI.GIPO26, Data_Lines.pin7, Data_Lines.pin34
  Address6: RPI.GIPO21, Data_Lines.pin8, Data_Lines.pin33
  Address7: RPI.GIPO20, Data_Lines.pin9, Data_Lines.pin32
  Broadcast: RPI.GIPO16, Data_Lines.pin1, Data_Lines.pin40
  GPIO12: RPI.GIPO12, Data_Lines.pin27
  SPI_CS: RPI.GIPO8, Data_Lines.pin17, Data_Lines.pin24
  ButtonUp: RPI.GIPO25, Remote_Display.pin5
  ButtonDown: RPI.GIPO24, Remote_Display.pin6
  ButtonBack: RPI.GIPO23, Remote_Display.pin12
  ButtonSelect: RPI.GIPO18, Remote_Display.pin11
  GPIO15: RPI.GIPO15, Data_Lines.pin31
  ButtonPWR: RPI.GIPO14, Remote_Display.pin13
  N1: LED1.anode, R1.Pin_0
