# Fritzing sketch PiezoFilter (saved by Fritzing 0.9.3b)
circuit board: 9.02988cm x 2.73043cm
breadboards: 1

parts:
  IN = MolexRow
  C104 = MolexRow
  C105 = MolexRow
  C106 = MolexRow
  OUT = MolexRow
  C108 = MolexRow
  C109 = MolexRow
  C110 = MolexRow
  L3 = 11PHC Inductance
  L6 = 11PHC Inductance
  L7 = 11PHC Inductance
  L1 = 11PHC Inductance
  L5 = 11PHC Inductance
  L2 = 11PHC Inductance
  L4 = 11PHC Inductance
  L8 = 11PHC Inductance

nets:
  N1: IN.connector0, L1.connector1
  N2: IN.connector1, L2.connector1
  N3: C104.connector0, L3.connector1
  N4: C104.connector1, L4.connector1
  N5: C105.connector0, L5.connector1
  N6: C105.connector1, L6.connector1
  N7: C106.connector0, L7.connector1
  N8: C106.connector1, L8.connector1
  N9: OUT.connector0, L1.connector0
  N10: OUT.connector1, L2.connector0
  N11: C108.connector0, L3.connector0
  N12: C108.connector1, L4.connector0
  N13: C109.connector0, L5.connector0
  N14: C109.connector1, L6.connector0
  N15: C110.connector0, L7.connector0
  N16: C110.connector1, L8.connector0

notes:
  x4 Filter Board R1
